// Logisim project TrafficConjuctionSystemSimulation.circ as structural Verilog: 1 circuit, main circuit main
module main (
  input  VIP2,
  input  VIP1,
  input  VIP3,
  input  VIP0
);

  wire and_1_out, and_2_out, and_3_out, and_4_out, and_5_out, and_6_out, and_7_out, and_8_out, and_9_out,
       and_10_out, and_11_out, and_12_out, and_13_out, and_14_out, and_15_out, and_16_out, and_17_out,
       and_18_out, and_19_out, and_20_out, and_21_out, and_22_out, and_23_out, and_24_out, and_25_out,
       and_26_out, and_27_out, and_28_out, and_29_out, and_30_out, and_31_out, and_32_out, Button0_out,
       Button1_out, Button2_out, Button3_out, button_1_out, Da0_q, Da1_q, Da2_q, Da3_q, Dg0_q, Dg1_q, Dg2_q,
       Dg3_q, Dr0_q, Dr1_q, Dr2_q, Dr2_qn, Dr3_q, not_1_out, not_2_out, not_3_out, not_4_out, not_5_out,
       not_6_out, not_7_out, not_8_out, not_9_out, not_10_out, not_11_out, not_12_out, not_13_out,
       not_14_out, not_15_out, or_1_out, or_2_out, or_3_out, or_4_out, or_5_out, or_6_out, or_7_out,
       or_8_out, or_9_out, or_10_out, or_11_out, or_12_out, xor_1_out, xor_2_out, xor_3_out, xor_4_out;

  D_Flip_Flop Dr0 (.clk(button_1_out), .D(xor_1_out), .Q(Dr0_q));  // open: Qn, preset, en, reset
  xor xor_1 (xor_1_out, Dr0_q, Da0_q);
  Button button_1 (.out(button_1_out));
  and and_1 (and_1_out, Dr0_q, Da0_q);
  not not_1 (not_1_out, or_5_out);
  and and_2 (and_2_out, Dg2_q, not_1_out);
  and and_3 (and_3_out, Da2_q, not_1_out);
  or or_1 (or_1_out, Dg0_q, and_23_out);
  not not_2 (not_2_out, Dr0_q);
  D_Flip_Flop Da0 (.clk(button_1_out), .D(or_1_out), .Q(Da0_q));  // open: Qn, preset, en, reset
  and and_4 (and_4_out, not_11_out, VIP2);
  not not_3 (not_3_out, VIP2);
  and and_5 (and_5_out, VIP3, not_3_out);
  and and_6 (and_6_out, VIP3, not_10_out);
  not not_4 (not_4_out, VIP3);
  or or_2 (or_2_out, or_5_out, Dr2_q);
  and and_7 (and_7_out, not_2_out, Da0_q);
  D_Flip_Flop Dr1 (.clk(button_1_out), .D(xor_2_out), .Q(Dr1_q));  // open: Qn, preset, en, reset
  xor xor_2 (xor_2_out, Dr1_q, Da1_q);
  and and_8 (and_8_out, VIP2, not_10_out);
  and and_9 (and_9_out, VIP2, not_4_out);
  and and_10 (and_10_out, not_11_out, VIP3);
  not not_5 (not_5_out, or_4_out);
  or or_3 (or_3_out, Dg1_q, and_7_out);
  and and_11 (and_11_out, Dr1_q, Da1_q);
  or or_4 (or_4_out, and_15_out, and_16_out, and_9_out);
  and and_12 (and_12_out, not_5_out, Dg3_q);
  and and_13 (and_13_out, not_5_out, Da3_q);
  not not_6 (not_6_out, Dr1_q);
  D_Flip_Flop Da1 (.clk(button_1_out), .D(or_3_out), .Q(Da1_q));  // open: Qn, preset, en, reset
  xor xor_3 (xor_3_out, Dr2_q, Da2_q);
  or or_5 (or_5_out, and_21_out, and_5_out, and_19_out);
  LED led_1 (.in(or_5_out));
  LED led_2 (.in(or_4_out));
  or or_6 (or_6_out, and_20_out, and_6_out, and_8_out);
  LED led_3 (.in(or_6_out));
  LED VIP (.in(or_7_out));
  or or_7 (or_7_out, and_10_out, and_4_out, and_22_out);
  or or_8 (or_8_out, or_4_out, Dr3_q);
  and and_14 (and_14_out, not_6_out, Da1_q);
  D_Flip_Flop Dr2 (.clk(button_1_out), .D(xor_3_out), .Q(Dr2_q), .Qn(Dr2_qn));  // open: preset, en, reset
  not not_7 (not_7_out, or_6_out);
  not not_8 (not_8_out, or_7_out);
  or or_9 (or_9_out, Dg2_q, and_14_out);
  D_Flip_Flop Da2 (.clk(button_1_out), .D(or_9_out), .Q(Da2_q));  // open: Qn, preset, en, reset
  and and_15 (and_15_out, VIP1, not_4_out);
  and and_16 (and_16_out, VIP0, not_4_out);
  and and_17 (and_17_out, Dr2_qn, Da2_q);
  and and_18 (and_18_out, Dr2_q, Da2_q);
  xor xor_4 (xor_4_out, Dr3_q, Da3_q);
  and and_19 (and_19_out, not_3_out, VIP0);
  and and_20 (and_20_out, VIP0, not_10_out);
  and and_21 (and_21_out, not_3_out, VIP1);
  and and_22 (and_22_out, VIP1, not_11_out);
  and and_23 (and_23_out, not_9_out, Da3_q);
  not not_9 (not_9_out, Dr3_q);
  or or_10 (or_10_out, and_17_out, Dg3_q);
  D_Flip_Flop Dr3 (.clk(button_1_out), .D(xor_4_out), .Q(Dr3_q));  // open: Qn, preset, en, reset
  D_Flip_Flop Da3 (.clk(button_1_out), .D(or_10_out), .Q(Da3_q));  // open: Qn, preset, en, reset
  not not_10 (not_10_out, VIP1);
  not not_11 (not_11_out, VIP0);
  and and_24 (and_24_out, Dr3_q, Da3_q);
  D_Flip_Flop Dg0 (.clk(button_1_out), .D(and_1_out), .Q(Dg0_q));  // open: Qn, preset, en, reset
  D_Flip_Flop Dg2 (.clk(button_1_out), .D(and_18_out), .Q(Dg2_q));  // open: Qn, preset, en, reset
  D_Flip_Flop Dg1 (.clk(button_1_out), .D(and_11_out), .Q(Dg1_q));  // open: Qn, preset, en, reset
  D_Flip_Flop Dg3 (.clk(button_1_out), .D(and_24_out), .Q(Dg3_q));  // open: Qn, preset, en, reset
  not not_12 (not_12_out, and_2_out);
  LED Traffic_Light_3_red (.in(or_8_out));
  LED PL3red (.in(not_12_out));
  LED Traffic_Light_3_amber (.in(and_13_out));
  LED PL3green (.in(and_2_out));
  LED Traffic_Light_3_green (.in(and_12_out));
  not not_13 (not_13_out, and_12_out);
  or or_11 (or_11_out, Dr0_q, or_7_out);
  and and_25 (and_25_out, Da1_q, not_7_out);
  and and_26 (and_26_out, not_7_out, Dg1_q);
  LED Traffic_Light_2_red (.in(or_2_out));
  LED Traffic_Light_2_amber (.in(and_3_out));
  LED Traffic_Light_2_green (.in(and_2_out));
  LED PL2green (.in(and_26_out));
  LED PL0red (.in(not_13_out));
  LED Traffic_Light_0_red (.in(or_11_out));
  LED Traffic_Light_0_amber (.in(and_29_out));
  LED Traffic_Light_0_green (.in(and_28_out));
  and and_27 (and_27_out, Dr0_q, Button0_out);
  and and_28 (and_28_out, not_8_out, Dg0_q);
  and and_29 (and_29_out, Da0_q, not_8_out);
  or or_12 (or_12_out, Dr1_q, or_6_out);
  LED PL2red (.in(not_14_out));
  LED PL1green (.in(and_28_out));
  LED PL1red (.in(not_15_out));
  LED PL0green (.in(and_12_out));
  LED Alarm1 (.in(and_27_out));
  LED Alarm2 (.in(and_30_out));
  and and_30 (and_30_out, Dr1_q, Button1_out);
  Button Button0 (.out(Button0_out));
  Button Button1 (.out(Button1_out));
  not not_14 (not_14_out, and_26_out);
  LED Traffic_Light_1_red (.in(or_12_out));
  LED Traffic_Light_1_amber (.in(and_25_out));
  LED Traffic_Light_1_green (.in(and_26_out));
  not not_15 (not_15_out, and_28_out);
  LED Alarm3 (.in(and_31_out));
  LED Alarm0 (.in(and_32_out));
  and and_31 (and_31_out, Dr2_q, Button2_out);
  and and_32 (and_32_out, Dr3_q, Button3_out);
  Button Button2 (.out(Button2_out));
  Button Button3 (.out(Button3_out));
endmodule
